// Digital circuit ALU.dig as structural Verilog
module ALU (
  input  [3:0] A,
  input  [3:0] B,
  input  S1,
  input  S0,
  input  Cin,
  output [3:0] D
);

  wire [3:0] multiplexer_1_out, not_1_out;

  assign not_1_out = ~B;  // Not not_1, 4 bits wide
  Multiplexer #(.Bits(4), .Selector_Bits(2)) multiplexer_1 (
    .sel({S1, S0}), .in_0(B), .in_1(not_1_out), .in_2(4'b0000), .in_3(4'b1111), .out(multiplexer_1_out));
  Add #(.Bits(4)) add_1 (.a(A), .b(multiplexer_1_out), .c_i(Cin), .s(D));  // open: c_o
endmodule
