// Digital circuit RegisterFile.dig as structural Verilog
module RegisterFile (
  input  [1:0] Read_Reg_1,
  input  [1:0] Read_Reg_2,
  input  [1:0] Write_Reg,
  input  [3:0] Write_Data,
  input  Write_Enable,
  input  clk,
  output [3:0] Read_Data_1,
  output [3:0] Read_Data_2
);

  wire and_1_out, and_2_out, and_3_out, and_4_out, decoder_1_out_0, decoder_1_out_1, decoder_1_out_2,
       decoder_1_out_3;
  wire [3:0] R0_q, R1_q, R2_q, R3_q;

  Decoder #(.Selector_Bits(2)) decoder_1 (
    .sel(Write_Reg), .out_0(decoder_1_out_0), .out_1(decoder_1_out_1), .out_2(decoder_1_out_2),
    .out_3(decoder_1_out_3));
  and and_1 (and_1_out, decoder_1_out_0, Write_Enable);
  and and_2 (and_2_out, decoder_1_out_1, Write_Enable);
  and and_3 (and_3_out, decoder_1_out_2, Write_Enable);
  and and_4 (and_4_out, decoder_1_out_3, Write_Enable);
  Register #(.Bits(4)) R0 (.D(Write_Data), .C(clk), .en(and_1_out), .Q(R0_q));
  Register #(.Bits(4)) R1 (.D(Write_Data), .C(clk), .en(and_2_out), .Q(R1_q));
  Register #(.Bits(4)) R2 (.D(Write_Data), .C(clk), .en(and_3_out), .Q(R2_q));
  Register #(.Bits(4)) R3 (.D(Write_Data), .C(clk), .en(and_4_out), .Q(R3_q));
  Multiplexer #(.Bits(4), .Selector_Bits(2)) multiplexer_1 (
    .sel(Read_Reg_1), .in_0(R0_q), .in_1(R1_q), .in_2(R2_q), .in_3(R3_q), .out(Read_Data_1));
  Multiplexer #(.Selector_Bits(2), .Bits(4)) multiplexer_2 (
    .sel(Read_Reg_2), .in_0(R0_q), .in_1(R1_q), .in_2(R2_q), .in_3(R3_q), .out(Read_Data_2));
endmodule
