// Digital circuit RegisterFile_ALU.dig as structural Verilog
module RegisterFile_ALU (
  input  [1:0] Read_Reg_1,
  input  [1:0] Read_Reg_2,
  input  [1:0] Write_Reg,
  input  Write_Enable,
  input  S0,
  input  S1,
  input  Cin,
  input  clk,
  input  [3:0] Manual_Data_In,
  input  Data_Source_Sel
);

  wire [3:0] alu_1_d, multiplexer_1_out, registerfile_1_read_data_1, registerfile_1_read_data_2;

  Multiplexer #(.Bits(4)) multiplexer_1 (
    .sel(Data_Source_Sel), .in_0(alu_1_d), .in_1(Manual_Data_In), .out(multiplexer_1_out));
  RegisterFile registerfile_1 (
    .Read_Reg_1(Read_Reg_1), .Read_Reg_2(Read_Reg_2), .Write_Reg(Write_Reg), .Write_Data(multiplexer_1_out),
    .Write_Enable(Write_Enable), .clk(clk), .Read_Data_1(registerfile_1_read_data_1),
    .Read_Data_2(registerfile_1_read_data_2));
  // Probe on registerfile_1_read_data_2
  // Probe on registerfile_1_read_data_1
  ALU alu_1 (.A(registerfile_1_read_data_1), .B(registerfile_1_read_data_2), .S1(S1), .S0(S0), .Cin(Cin), .D(alu_1_d));
  // Probe on alu_1_d
endmodule
